// Logisim project pratica4.circ as structural Verilog: 1 circuit, main circuit main
module main (
  input  a,
  input  b,
  input  c,
  input  d,
  input  a_prime,
  input  b_prime,
  input  c_prime,
  input  d_prime,
  input  X0,
  input  X1,
  input  Y0,
  input  Y1,
  input  a_2,
  input  b_2,
  input  a_3,
  input  b_3,
  input  c_2,
  input  d_2,
  input  in_19,
  output out_20,
  output out_21,
  output out_22,
  output out_23
);

  wire and_1_out, and_2_out, and_4_out, and_5_out, gerador_out, not_1_out, not_2_out, not_3_out, verif_out,
       xnor_1_out, xnor_2_out;

  not not_1 (not_1_out, a_2);
  not not_2 (not_2_out, b_2);
  not not_3 (not_3_out, a_3);
  ExactlyOne gerador (.out(gerador_out), .in0(a), .in1(b), .in2(c), .in3(d));
  xnor xnor_1 (xnor_1_out, X0, Y0);
  xnor xnor_2 (xnor_2_out, X1, Y1);
  and and_1 (and_1_out, not_1_out, b_2);
  and and_2 (and_2_out, a_2, not_2_out);
  ExactlyOne verif (.out(verif_out), .in0(a_prime), .in1(b_prime), .in2(c_prime), .in3(d_prime));
  and and_3 (out_21, xnor_1_out, xnor_2_out);
  or or_1 (out_22, and_1_out, and_2_out);
  and and_4 (and_4_out, not_3_out, c_2, d_2);
  and and_5 (and_5_out, not_3_out, b_3);
  xnor xnor_3 (out_20, gerador_out, verif_out);
  or or_2 (out_23, and_4_out, and_5_out);

  // Notes on the sheet:
  //   Questão 1
  //   Questão 2
  //   Questão 3
  //   Questão 4
  //   P
  //   P'
endmodule
