// Logisim project pratica2.circ as structural Verilog
module main (
  input  A,
  input  B,
  input  C,
  input  D,
  input  A_2,
  input  B_2,
  input  C_2,
  input  a_3,
  input  b_3,
  input  c_3,
  input  a_4,
  input  b_4,
  input  c_4,
  input  a_5,
  input  b_5,
  input  c_5,
  input  d_2,
  input  e,
  input  a_6,
  input  b_6,
  input  c_6,
  input  d_3,
  input  e_2,
  input  a_7,
  input  b_7,
  input  c_7,
  input  c_8,
  input  f,
  input  in_29,
  output out_30,
  output X,
  output Y,
  output x_2,
  output out_34,
  output out_35,
  output out_36,
  output x_3,
  output p,
  output r,
  output m,
  output b_8,
  output s
);

  wire and_1_out, and_2_out, and_3_out, and_4_out, and_5_out, and_6_out, and_7_out, and_9_out, and_11_out,
       and_12_out, and_15_out, nand_1_out, nand_2_out, nand_3_out, nand_4_out, nand_5_out, nand_6_out,
       nand_7_out, nand_8_out, nand_9_out, nand_11_out, nand_12_out, nand_13_out, nand_14_out, not_1_out,
       not_2_out, not_3_out, not_4_out, not_5_out, not_6_out, not_7_out, not_8_out, not_9_out, not_10_out,
       not_11_out, not_12_out, not_13_out, or_3_out, xor_1_out, xor_2_out;

  not not_1 (not_1_out, A);
  not not_2 (not_2_out, B_2);
  not not_3 (not_3_out, B);
  not not_4 (not_4_out, B_2);
  not not_5 (not_5_out, b_3);
  not not_6 (not_6_out, c_3);
  nand nand_1 (nand_1_out, b_4, b_4);
  nand nand_2 (nand_2_out, c_4, c_4);
  not not_7 (not_7_out, d_2);
  not nand_3 (nand_3_out, d_3);  // NAND_Gate
  not not_8 (not_8_out, b_7);
  not not_9 (not_9_out, c_7);
  not not_10 (not_10_out, c_8);
  not not_11 (not_11_out, f);
  not not_12 (not_12_out, c_8);
  not not_13 (not_13_out, f);
  and and_1 (and_1_out, A, B);
  and and_2 (and_2_out, not_1_out, C);
  and and_3 (and_3_out, not_3_out, C);
  and and_4 (and_4_out, B, not_3_out, D);
  xor xor_1 (xor_1_out, A_2, not_2_out);
  and and_5 (and_5_out, A_2, C_2);
  and and_6 (and_6_out, A_2, B_2);
  and and_7 (and_7_out, not_4_out, C_2);
  and and_8 (x_2, a_3, not_5_out, not_6_out);
  nand nand_4 (nand_4_out, a_5, b_5);
  nand nand_5 (nand_5_out, a_6, b_6);
  not nand_6 (nand_6_out, e_2);  // NAND_Gate
  and and_9 (and_9_out, not_8_out, not_9_out);
  and and_10 (p, c_8, f);
  and and_11 (and_11_out, not_10_out, f);
  and and_12 (and_12_out, c_8, not_11_out);
  and and_13 (b_8, not_12_out, not_13_out);
  not not_14 (s, c_8);
  or or_1 (X, xor_1_out, and_5_out);
  or or_2 (Y, and_6_out, and_7_out);
  nand nand_7 (nand_7_out, a_4, nand_1_out, nand_2_out);
  xor xor_2 (xor_2_out, nand_4_out, c_5);
  or or_3 (or_3_out, not_7_out, e);
  nand nand_8 (nand_8_out, nand_5_out, c_6);
  nand nand_9 (nand_9_out, nand_3_out, nand_6_out);
  or or_4 (r, f, c_8);
  or or_5 (m, and_11_out, and_12_out);
  or or_6 (out_30, and_1_out, and_2_out, and_3_out, and_4_out);
  not nand_10 (out_34, nand_7_out);  // NAND_Gate
  and and_14 (out_35, xor_2_out, or_3_out);
  nand nand_11 (nand_11_out, nand_5_out, nand_8_out);
  nand nand_12 (nand_12_out, nand_8_out, c_6);
  and and_15 (and_15_out, a_7, b_7, c_7);
  nand nand_13 (nand_13_out, nand_11_out, nand_12_out);
  or or_7 (x_3, and_15_out, and_9_out);
  nand nand_14 (nand_14_out, nand_13_out, nand_9_out);
  not nand_15 (out_36, nand_14_out);  // NAND_Gate

  // Notes on the sheet:
  //   1.1
  //   1.2
  //   1.3
  //   b)
  //   c)
  //   1.4
  //   1.5
  //   b)
  //   c)
  //   Circuito 1
  //   a) A * B' * C'
  //   c)
  //   Circuito 2
  //   p = c * f
  //   r  = f + c
  //   b = c' * f'
  //   s = c'
  //   a) ((A' + B)' [xor] C) * (D' + E)
  //   a)[ Enviado separadamente]
  //   m = c' * f + c * f'
  //   b) Não há como simplificar a expressão, logo o circuito é o mesmo:
endmodule

module auxiliar2 (
  input  c,
  input  f,
  output p,
  output r,
  output m,
  output b,
  output s
);

  wire and_2_out, and_3_out, not_1_out, not_2_out, not_3_out, not_4_out;

  and and_1 (p, c, f);
  or or_1 (r, f, c);
  not not_1 (not_1_out, c);
  not not_2 (not_2_out, f);
  not not_3 (not_3_out, c);
  not not_4 (not_4_out, f);
  not not_5 (s, c);
  and and_2 (and_2_out, not_1_out, f);
  and and_3 (and_3_out, c, not_2_out);
  and and_4 (b, not_3_out, not_4_out);
  or or_2 (m, and_2_out, and_3_out);
endmodule
