// Logisim project pratica6.circ as structural Verilog: 3 circuits, main circuit main
module main (
  input  A,
  input  B,
  input  SELETOR_1,
  input  SELETOR_0,
  input  C,
  input  D,
  input  X,
  input  SELETOR,
  input  Y,
  input  SELETOR_1_2,
  input  SELETOR_0_2,
  input  E,
  input  SELETOR_2,
  input  E_2,
  input  [3:0] in_15,
  input  in_16,
  output S,
  output S_2,
  output A_2,
  output B_2,
  output C_2,
  output D_2,
  output X_2,
  output Y_2,
  output out_25
);

  wire and_1_out, and_2_out, demux_1_2_1_x, demux_1_2_1_y, MUX_2_1_2_s, MUX_2_1_s, not_1_out, not_2_out;

  demux_1_2 demux_1_2_1 (.SELETOR(SELETOR_1_2), .E(E), .X(demux_1_2_1_x), .Y(demux_1_2_1_y));
  mux_2_1 MUX_2_1 (.X(A), .SELETOR(SELETOR_1), .Y(B), .S(MUX_2_1_s));
  mux_2_1 MUX_2_1_2 (.X(C), .SELETOR(SELETOR_1), .Y(D), .S(MUX_2_1_2_s));
  and and_1 (and_1_out, X, not_1_out);
  not not_1 (not_1_out, SELETOR);
  and and_2 (and_2_out, SELETOR, Y);
  not not_2 (not_2_out, SELETOR_2);
  and and_3 (X_2, not_2_out, E_2);
  and and_4 (Y_2, E_2, SELETOR_2);
  Multiplexer #(.select(4)) multiplexer_1 (
    .in0(1'b0), .in1(1'b0), .in2(1'b0), .in3(1'b0), .in4(1'b1), .in5(1'b1), .in6(1'b1), .in7(1'b1),
    .in8(1'b1), .in9(1'b0), .in10(1'b0), .in11(1'b0), .in12(1'b0), .in13(1'b1), .in14(1'b1), .in15(1'b1),
    .out(out_25), .sel(in_15));  // open: en
  or or_1 (S_2, and_1_out, and_2_out);
  mux_2_1 MUX_2_1_3 (.X(MUX_2_1_s), .SELETOR(SELETOR_0), .Y(MUX_2_1_2_s), .S(S));
  demux_1_2 demux_1_2_2 (.SELETOR(SELETOR_0_2), .E(demux_1_2_1_x), .X(A_2), .Y(B_2));
  demux_1_2 demux_1_2_3 (.SELETOR(SELETOR_0_2), .E(demux_1_2_1_y), .X(C_2), .Y(D_2));

  // Notes on the sheet:
  //   1.
  //   2.
  //   3.
  //   CONSTRUÇÃO MUX 4:1 A PARTIR DE MUX 2:1
  //   CONSTRUÇÃO MUX 2:1
  //   CONSTRUÇÃO DEMUX 1:4 A PARTIR DE DEMUX 1:2
  //   CONSTRUÇÃO DEMUX 1:2
endmodule

module mux_2_1 (
  input  X,
  input  SELETOR,
  input  Y,
  output S
);

  wire and_1_out, and_2_out, not_1_out;

  not not_1 (not_1_out, SELETOR);
  and and_1 (and_1_out, X, not_1_out);
  and and_2 (and_2_out, SELETOR, Y);
  or or_1 (S, and_1_out, and_2_out);
endmodule

// DEMUX 1:2
module demux_1_2 (
  input  SELETOR,
  input  E,
  output X,
  output Y
);

  wire not_1_out;

  not not_1 (not_1_out, SELETOR);
  and and_1 (X, not_1_out, E);
  and and_2 (Y, E, SELETOR);
endmodule
